# Fritzing sketch sketch (saved by Fritzing 0.9.4)

parts:
  M1 = DOIT Esp32 DevKit v1 (30 pins long, 11 pins width) [part_number=ESP32S-PIN30]
  Part1 = Adafruit CCS811
  LED1 = RGB LED (com. cathode, rgb) [package="5 mm [THT]"]
  R2 = Resistor [tolerance=±5% resistance=220 package=THT]
  R3 = Resistor [tolerance=±5% resistance=220 package=THT]
  R4 = Resistor [tolerance=±5% resistance=220 package=THT]

nets:
  GND: M1.GND, Part1.GND, LED1.common_cathode
  N1: M1.D15, R2.Pin_1
  N2: M1.D2, R3.Pin_1
  N3: M1.D4, R4.Pin_1
  N4: M1.D21, Part1.SDA
  N5: M1.D22, Part1.SCL
  VIN: M1.VIN, Part1.VIN
  N6: LED1.red_anode, R2.Pin_0
  N7: LED1.green_anode, R3.Pin_0
  N8: LED1.blue_anode, R4.Pin_0

custom parts:
  DOIT Esp32 DevKit v1 (30 pins long, 11 pins width): The DOIT Esp32 DevKit v1 is one of the development board created by DOIT to evaluate the ESP-WROOM-32 module. It is based on the ESP32 microcontroller that boasts Wifi, Bluetooth, Ethernet and Low Power support all in a single chip. (vanepp) made breadboard work, adjusted pin numbering and labels and reduced size of schematic and cleaned up pcb. This chip is 30pins long (2 x15) and 11 pins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
